# Fritzing sketch shootSB (saved by Fritzing 0.9.3b)
circuit board: 3.4cm x 3.4cm
breadboards: 1

parts:
  BATTERY_PACK_~11v = Battery block 9V  # not connected
  UBEC1 = Mystery Part - 4 pins [package=THT]  # not connected
  IR_1_5R = Resistor [tolerance=±5% resistance=220 package=THT]
  RB = Resistor [tolerance=±5% resistance=220 package=THT]
  RG = Resistor [tolerance=±5% resistance=220 package=THT]
  RR = Resistor [tolerance=±5% resistance=220 package=THT]
  LED3 = LED - 5mm [color="Infrared (940nm)" package="5 mm [THT]"]
  R = female pin header, 1 pin [form="♀ (female)"]
  G = female pin header, 1 pin [form="♀ (female)"]
  CA = female pin header, 1 pin [form="♀ (female)"]
  B = female pin header, 1 pin [form="♀ (female)"]
  LED = Pad [width=4.9453028210682612 height=4.3625693181823859 connect=center]  # not connected
  SHOOT = female pin header, 5 pins [form="♀ (female)"]

nets:
  N1: IR_1_5R.Pin_0, SHOOT.pin2
  N2: IR_1_5R.Pin_1, LED3.cathode
  N3: RB.Pin_0, B.pin1
  N4: RB.Pin_1, SHOOT.pin3
  N5: RG.Pin_0, G.pin1
  N6: RG.Pin_1, SHOOT.pin4
  N7: RR.Pin_0, R.pin1
  N8: RR.Pin_1, SHOOT.pin5
  N9: LED3.anode, CA.pin1, SHOOT.pin1

notes:
  Battery Monitoring Voltage divider
  Sensor PCB
  This line links arduino and battery grounds
  S + -
  I

custom parts:
  Mystery Part - 4 pins: A dummy, proxy, ersatz, stand-in part for whatever you want. With 4 pins on a 100 mil inline pin header footprint.

// code stored in the sketch: IRcomms.ino
//The IR communication components.
//
// Hacked together by Andrew Shirley

// Code which was either 'copypasta'ed or used as inspiration at some point:
//
// http://www.arduino.cc/cgi-bin/yabb2/YaBB.pl?num=1240843250 Copyright (C) Timo Herva aka 'mettapera', 2009
// http://tthheessiiss.wordpress.com/2009/08/05/dirt-cheap-wireless/ 

//NB. as these are quite time intensive enabling this often breaks it :-(
//#define DEBUG_SEND 1
//#define DEBUG_RECV 1

// pin numbers (9 is used for a Carrier wave and so isn't available)
#define pin_infrared 8 // ir LED
#define pin_ir_feedback 13 // normal LED
#define pin_ir_reciever_port PINB  // These 2 equate to pin 12
#define pin_ir_reciever_bit 4      // "           "          "
#define pin_ir_reciever 12         // normal LED

// some timings
long headerDuration = 2400;
long intervalDuration = 600;
long oneDuration = 1200;
long zeroDuration = 600;

byte timingTolerance = 100;

////////////////////////
// IR Writing variables
unsigned long writeBuffer = 0;
byte writeBits = 0;
unsigned long writeUpTime = 0;
unsigned long writeDownTime = 0;
unsigned long writeLastChangeTime = 0;

////////////////////////
// IR reading variables
unsigned long readBuffer = 0;
byte bitsRead = 0;

byte oldPinValue = 0;

//the micros for the point at which the IR went high
unsigned long readRiseTime = 0;

//the micros for the point at which the IR went low
unsigned long readFallTime = 0;

////////////////////////
// IR reading functions

//read the IR receiver and if applicable add to the readBuffer. This will return 1 if the transmission appears to be complete. Subsequent reads will return 0.
int signal_recieve() {
  byte pinValue = ! bitRead(pin_ir_reciever_port, pin_ir_reciever_bit);

  if (!oldPinValue && pinValue) {
    //IR rising edge
    readRiseTime = micros();
    oldPinValue = HIGH;
#ifdef DEBUG_RECV
    Serial.print("\\ @");
    Serial.println(readRiseTime);
#endif
    //there is always more to be read if the IR is high.
    return 0;
  }
  else if (oldPinValue && !pinValue) {
    //IR falling edge
    readFallTime = micros();
    unsigned long duration = readFallTime - readRiseTime;

    if (within_tolerance(duration, headerDuration, timingTolerance)) {
      //we are within tolerance of 2400 us - a restart
      readBuffer = 0;
      bitsRead = 0;
#ifdef DEBUG_RECV
      Serial.println("--");
#endif
    }
    else if (within_tolerance(duration, oneDuration, timingTolerance)) {
      //we are within tolerance of 1200 us - a one
      readBuffer = (readBuffer << 1) + 1;
      bitsRead++;
#ifdef DEBUG_RECV
      Serial.println("-1");
#endif
    }
    else if (within_tolerance(duration, zeroDuration, timingTolerance)) {
      //we are within tolerance of 600 us - a zero
      readBuffer = readBuffer << 1;
      bitsRead++;
#ifdef DEBUG_RECV
      Serial.println("-0");
#endif
    }
    else {
#ifdef DEBUG_RECV
      Serial.print("/ @");
      Serial.print(readFallTime);
      Serial.print("  ");
      Serial.println(duration);
#endif
    }

    oldPinValue = LOW;
    //wait to see if there is more to be read
    return 0;
  }
  else if (oldPinValue) {
    //IR continues to be high
    //there is always more to be read if the IR is high.
    return 0;
  }
  else /*if (!oldPinValue)*/ {
    //IR continues to be low
    //if we have been low for more than interval + tolerance (twice for extra leniency) we can assume the transmission has finished and try to read it.
    if (!readFallTime) {
      //we aren't waiting for an interval, all quiet on the IR front.
      return 0;
    }
    else if (micros() - readFallTime > intervalDuration + timingTolerance * 2) {
      readFallTime = 0; //cache this result
#ifdef DEBUG_RECV
      Serial.println("xx");
#endif
      return 1;
    }
    else {
      //still low, waiting for the interval
      return 0;
    }
  }
}

boolean within_tolerance(unsigned long value, unsigned long target, byte tolerance) {
  long remainder = value - target;
  return remainder < tolerance && remainder > -tolerance;
}

////////////////////////
// IR writing functions

void start_command(unsigned long command) {
  if (writeUpTime || writeDownTime) {
    //already writing - this is an error
    //Serial.println("tried to start a command when we are already sending");
    return;
  }

  command = reverse(command, 16);
  writeBuffer = addParityBit(command);
  writeBits = 17;

  //write header
  ir_up();
#ifdef DEBUG_SEND
  Serial.println("  \\");
#endif
  writeDownTime = headerDuration;
}

void signal_send() {
  unsigned long elapsed = micros() - writeLastChangeTime;
  
  if (writeDownTime && writeDownTime <= elapsed) {
#ifdef DEBUG_SEND
    Serial.print("  /");
    Serial.print(elapsed);
    Serial.print(" - ");
    Serial.println(writeDownTime, DEC);
#endif
    ir_down();
    writeDownTime = 0;
    
    if (writeBits) {
      //not done yet
      writeUpTime = intervalDuration;
    }
  }
  else if (writeUpTime && writeUpTime <= elapsed) {
#ifdef DEBUG_SEND
    Serial.print("  \\");
    Serial.print(elapsed);
    Serial.print(" - ");
    Serial.println(writeUpTime, DEC);
#endif
    ir_up();
    writeUpTime = 0;
    
    if (writeBuffer & B1) {
      //write a one
      writeDownTime = oneDuration;
    }
    else {
      //write a zero
      writeDownTime = zeroDuration;
    }
    
    writeBuffer = writeBuffer >> 1;
    writeBits--;
  }
}

void ir_up() {
  digitalWrite(pin_infrared, HIGH);
  digitalWrite(pin_ir_feedback, HIGH);
  writeLastChangeTime = micros();
}

void ir_down() {
  digitalWrite(pin_infrared, LOW);
  digitalWrite(pin_ir_feedback, LOW);
  writeLastChangeTime = micros();
}

/*
 * Reverse the num least significant bits.
 */
unsigned long reverse(unsigned long in, int num) {
  unsigned long out = 0;
  for (int i = 0; i < num; i++) {
    out = out << 1;
    out = out | (in & 1); //take the lsb from in to out
    in = in >> 1;
  }
  
  return out;
}

unsigned long timeCache = 0;

void timeDebug() {
  if (timeCache == 0) {
    timeCache = micros();
  }
  else {
    Serial.println(micros() - timeCache);
    timeCache = 0;
  }
}

// code stored in the sketch: main.ino
//#define DEBUG_DECODE 1

void decode_signal() {
#ifdef DEBUG_DECODE
  Serial.print("==");
  Serial.println(readBuffer, BIN);
  Serial.println(readBuffer, HEX);
#endif
}

//setting things ready
void setup() {
  //set the pins
  pinMode(pin_infrared, OUTPUT);
  pinMode(9, OUTPUT);
  pinMode(pin_ir_feedback, OUTPUT);
  pinMode(pin_ir_reciever, INPUT);
  
  // see http://www.atmel.com/dyn/resources/prod_documents/doc8161.pdf for more details (page 136 onwards)
  //set the carrier wave frequency. This only sets up pin 9.
  TCCR1A = _BV(COM1A0); // | _BV(COM1B0); for another pin (10)
  TCCR1B = _BV(WGM12) | _BV(CS10);
  
  TIMSK1 = 0; //no interupts
  TIFR1 = _BV(OCF1A) | _BV(OCF1A); //clear Output Compare Match Flags (by setting them :-P )
  unsigned long desired_freq = 40000;
  OCR1A = 10000000/desired_freq - 1; // see page 126 of datasheet for this equation
  //OCR1B = 10000000/desired_freq - 1; for another pin (10)

  ir_down();

  //debug  
  Serial.begin(9600);
}


unsigned long time = micros();

void loop() {
  if (micros() > time + 1000000) {
    time = micros();
    mt_fireShot();
  }

  signal_send();
  if (signal_recieve()) {
    decode_signal();
    mt_parseIRMessage(readBuffer);
  }
}

// code stored in the sketch: miles_tag_defines.ino

#define SYSTEM_MESSAGE                      B000

#define SYSTEM_MESSAGE_MASK                 0x1f00 // i.e. 5 least significant bits of the most significant byte
#define SYSTEM_MESSAGE_SHIFT                8

#define SYSTEM_MESSAGE_ADD_HEALTH           B00001
#define SYSTEM_MESSAGE_ADD_ROUNDS           B00010
#define SYSTEM_MESSAGE_ADD_CLIPS            B00011
#define SYSTEM_MESSAGE_ADD_RPG_ROUNDS       B00100

#define SYSTEM_MESSAGE_GOD_GUN              B01001

#define SYSTEM_MESSAGE_SCORE_DATA_HEADER    B10000
#define SYSTEM_MESSAGE_SCORE_REQUEST        B10001

#define SYSTEM_MESSAGE_SET_TEAM_ID          B10110
#define SYSTEM_MESSAGE_SET_PLAYER_ID        B10111

#define GOD_GUN_KILL_PLAYER                 0x00
#define GOD_GUN_PAUSE_PLAYER                0x01

#define GOD_GUN_START_GAME                  0x03
#define GOD_GUN_RESPAWN_PLAYER              0x04
#define GOD_GUN_INIT_PLAYER                 0x05
#define GOD_GUN_FULL_AMMO                   0x06
#define GOD_GUN_END_PLAYER                  0x07

#define UNLIMITED_CLIPS                     255
#define UNLIMITED_AMMO                      255


#define MT1_TEAM_MASK                       0xe000 // i.e. 3 most significant bits
#define MT1_TEAM_OFFSET                     13 // i.e. 3 most significant bits
#define MT1_PLAYER_MASK                     0x1f00 // i.e. 5 least significant bits of the most significant byte
#define MT1_PLAYER_OFFSET                   8 // i.e. 5 least significant bits of the most significant byte

#define MT1_DAMAGE_RESURRECT_OPPONENT       -1

// code stored in the sketch: miles_tag_gun_logic.ino
//milestag protocol 1 documented at http://www.lasertagparts.com/mtformat.htm
//milestag protocol 2 documented at http://www.lasertagparts.com/mtformat-2.htm
// we currently only implement MT1 as MT2 seems incomplete.

void serialPrint(int size, const char * fmt, ...) {
  char* out = (char*) malloc(size);
  va_list ap;
  va_start(ap, fmt);
  
  vsnprintf(out, size, fmt, ap);
  Serial.println(out);
  free(out);
  
  va_end (ap);
}

void mt_parseIRMessage(unsigned long recvBuffer) {
    if (!isEvenParity(recvBuffer)) {
        serialPrint(14, "Shot(Corrupt)");
        return;
    }

    //trim the 17th bit (parity) off to make things neater
    recvBuffer = recvBuffer >> 1;

    byte recv_TeamID = (recvBuffer & MT1_TEAM_MASK) >> MT1_TEAM_OFFSET;
    byte DataByte2 = recvBuffer & 0xff;

    if (recv_TeamID == SYSTEM_MESSAGE) {
        byte recv_SystemMessage = (recvBuffer & SYSTEM_MESSAGE_MASK) >> SYSTEM_MESSAGE_SHIFT;
        
        switch (recv_SystemMessage) {
            case SYSTEM_MESSAGE_SET_TEAM_ID:
                serialPrint(19, "Shot(SetTeam(%u))", DataByte2);
                break;
            case SYSTEM_MESSAGE_SET_PLAYER_ID:
                serialPrint(21, "Shot(SetPlayer(%u))", DataByte2);
                break;
            case SYSTEM_MESSAGE_ADD_HEALTH:
                serialPrint(21, "Shot(AddHealth(%u))", DataByte2);
                break;
            case SYSTEM_MESSAGE_ADD_CLIPS:
            {
                serialPrint(20, "Shot(AddClips(%u))", DataByte2);
                break;
            }
            case SYSTEM_MESSAGE_GOD_GUN:
            {
                byte recv_GodGun = DataByte2;
                switch (recv_GodGun) {
                    case GOD_GUN_KILL_PLAYER:
                        serialPrint(15, "Shot(Killed())");
                        break;
                    case GOD_GUN_FULL_AMMO:
                        serialPrint(17, "Shot(FullAmmo())");
                        break;
                    case GOD_GUN_RESPAWN_PLAYER:
                        serialPrint(15, "Shot(ReSpawn())");
                        break;
                    case GOD_GUN_PAUSE_PLAYER:
                    case GOD_GUN_START_GAME:
                    case GOD_GUN_INIT_PLAYER:
                    case GOD_GUN_END_PLAYER:
                    default:
                        serialPrint(17, "Shot(UnknownGGM)");
                        break;
                }
                
                break;
            }
            case SYSTEM_MESSAGE_ADD_ROUNDS:
                serialPrint(21, "Shot(AddRounds(%u))", DataByte2);
                break;
            case SYSTEM_MESSAGE_ADD_RPG_ROUNDS:
            case SYSTEM_MESSAGE_SCORE_DATA_HEADER:
            case SYSTEM_MESSAGE_SCORE_REQUEST:
            default:
                serialPrint(28, "Shot(UnknownSM(%lu))", recvBuffer);
                break;
        }
    } else {
        byte recv_PlayerID = (recvBuffer & MT1_PLAYER_MASK) >> MT1_PLAYER_OFFSET;
        signed char damage;
        
        byte recv_PlayerWeaponHit = DataByte2;
        switch (recv_PlayerWeaponHit) {
            case 0:
            {
                damage = MT1_DAMAGE_RESURRECT_OPPONENT;
                break;
            }
            case 1 ... 100:
            {
                damage = recv_PlayerWeaponHit;
                break;
            }
            //No 'Base' Mode
            /*case 101 ... 200:
            {
                recv_PlayerWeaponHit -= 100;
                baseDamage = recv_PlayerWeaponHit;
            }
            case 255:
                baseDamage = MT1_DAMAGE_RESURRECT_ENEMY_BASE;
            */

            default:
                serialPrint(17, "Shot(UnknownDmg)");
                break;
        }
        
        serialPrint(23, "Shot(Hit(%u,%u,%u))", recv_PlayerID, recv_TeamID, damage/*, baseDamage*/);
    }
}


void mt_fireShot() {
//  unsigned long shot = (TeamID << MT1_TEAM_OFFSET) | (PlayerID << MT1_PLAYER_OFFSET) | GunDamage;
  unsigned long shot = (0x01l << MT1_TEAM_OFFSET) | (0x01l << MT1_PLAYER_OFFSET) | 0x03l;

  //serialPrint(20, "shot: %ul", shot);

  start_command(shot);
}

// code stored in the sketch: parity.ino

boolean isEvenParity(unsigned long buf) {
  boolean evenParityBit = false;
  for (int i = 0; i < sizeof(unsigned long) * 8; i++) {
    evenParityBit = evenParityBit ^ (buf & 1);
    buf = buf >> 1;
  }
  return !evenParityBit;
}

unsigned long addParityBit(unsigned long in) {
  if (!isEvenParity(in)) {
    return in | 0x00010000;
  }
  else {
    return in;
  }
}
