# Fritzing sketch electronics3 (saved by Fritzing 0.7.7b)
breadboards: 1

parts:
  Arduino1 = Arduino
  Raspi_Power_Relay = Relay [part_number=FRS1B-S package=THT]
  Back_EMF_Diode = Rectifier Diode [part_number=1N4001 package="300 mil [THT]"]
  0_1uF = Electrolytic Capacitor [capacitance=10nF package="100 mil [THT, electrolytic]"]
  100R = Resistor [tolerance=±5% resistance=220 package=THT]
  J1 = male pin header, 3 pins [form="♂ (male)"]
  BATTERY_PACK_~11v = Battery block 9V  # not connected
  UBEC1 = Mystery Part - 4 pins [package=THT]  # not connected
  DIV_1_5K = 220 Ω Resistor [package=THT]
  DIV_2_4K = 220 Ω Resistor [package=THT]
  R2 = Resistor [tolerance=±5% resistance=10k package=THT]
  R3 = Resistor [tolerance=±5% resistance=10k package=THT]
  Q2 = Basic FET N-Channel [package="TO220 [THT]"]
  Q3 = Basic FET P-Channel [package="TO220 [THT]"]
  Q4 = Basic FET P-Channel [package="TO220 [THT]"]
  Q5 = Basic FET P-Channel [package="TO220 [THT]"]
  Q6 = Basic FET P-Channel [package="TO220 [THT]"]
  Q7 = Basic FET P-Channel [package="TO220 [THT]"]
  Q8 = Basic FET P-Channel [package="TO220 [THT]"]
  DC_Power1 = DC Power [voltage=12]
  D1 = Rectifier Diode [part_number=1N4001 package="300 mil [THT]"]
  D2 = Rectifier Diode [part_number=1N4001 package="300 mil [THT]"]
  D3 = Rectifier Diode [part_number=1N4001 package="300 mil [THT]"]
  D4 = Rectifier Diode [part_number=1N4001 package="300 mil [THT]"]
  R4 = Resistor [tolerance=±5% resistance=10 package=THT]
  LED1 = LED - 5mm [color="Green (560nm)" package="5 mm [THT]"]
  TIP127 = NPN-Transistor [package="TO92 [THT]"]
  R5 = Resistor [tolerance=±5% resistance=1.5k package=THT]
  C4 = Ceramic Capacitor [capacitance=0.47mF package="100 mil [THT, multilayer]"]
  Part1 = RJ45
  Part3 = RJ45  # not connected
  T1 = LM35 Temperature Sensor [package="TO92 [THT]"]
  5V_Power_in = Screw terminal - 2 pins [package=THT]
  HV_in = screw terminal, 4 pins
  UBEC_OUT = Screw terminal - 2 pins [package=THT]
  J2 = female pin header, 5 pins [form="♀ (female)"]
  J4 = female pin header, 2 pins [form="♀ (female)"]
  J5 = female pin header, 2 pins [form="♀ (female)"]
  J3 = female pin header, 5 pins [form="♀ (female)"]
  J6 = female pin header, 5 pins [form="♀ (female)"]

nets:
  N1: Arduino1.GND, Raspi_Power_Relay.COIL1, Back_EMF_Diode.anode, DIV_2_4K.Pin_1, R2.Pin_1, R3.Pin_1, Q2.source, Q3.source, Q4.source, Q5.source, Q6.source, Q7.source, Q8.source, 5V_Power_in.pin2, HV_in.pin2, HV_in.pin4, UBEC_OUT.pin2, J2.pin3, J5.pin1, J6.pin2
  N2: Arduino1.D13, Q4.gate
  N3: Arduino1.D12, Q3.gate
  N4: Arduino1.D11, Q2.gate
  N5: Arduino1.D10, Raspi_Power_Relay.COIL2, Back_EMF_Diode.cathode
  N6: Arduino1.D9, Q8.gate
  N7: Arduino1.D8, J2.pin2
  N8: Arduino1.D7, J6.pin1
  N9: Arduino1.D6, Q7.gate
  N10: Arduino1.D5, Q6.gate
  N11: Arduino1.D4, Q5.gate
  N12: Arduino1.D3, R2.Pin_0, J2.pin5
  N13: Arduino1.D2, R3.Pin_0, J4.pin2
  N14: Arduino1.A0, DIV_1_5K.Pin_1, DIV_2_4K.Pin_0
  N15: Raspi_Power_Relay.C1, Raspi_Power_Relay.C2, HV_in.pin1, HV_in.pin3
  N16: Raspi_Power_Relay.B, DIV_1_5K.Pin_0, UBEC_OUT.pin1
  N17: 0_1uF.-, J1.pin3, T1.GND
  N18: 0_1uF.+, J1.pin1, T1.+Vs
  N19: 100R.Pin_0, J1.pin2
  N20: 100R.Pin_1, T1.Vout
  N21: Q3.drain, J6.pin5
  N22: Q4.drain, J6.pin4
  N23: Q5.drain, J3.pin5
  N24: Q6.drain, J3.pin4
  N25: Q7.drain, J3.pin3
  N26: Q8.drain, J3.pin2
  N27: DC_Power1.V+, D1.cathode, D2.anode
  N28: DC_Power1.GND, D3.cathode, D4.anode
  N29: D1.anode, D3.anode
  N30: D2.cathode, D4.cathode, R4.Pin_0, LED1.anode
  N31: R4.Pin_1, TIP127.B
  N32: LED1.cathode, TIP127.E, R5.Pin_0
  N33: TIP127.C, C4.1, Part1.pin_4
  N34: R5.Pin_1, C4.0, Part1.pin_5
  N35: 5V_Power_in.pin1, J2.pin1, J2.pin4, J4.pin1, J5.pin2, J3.pin1, J6.pin3

notes:
  Battery Monitoring Voltage divider
  Sensor PCB
  This line links arduino and battery grounds
  S + -

custom parts:
  Mystery Part - 4 pins: A dummy, proxy, ersatz, stand-in part for whatever you want. With 4 pins on a 100 mil inline pin header footprint.
  220 Ω Resistor: A generic resistor (0.25W)
  220 Ω Resistor: A generic resistor (0.25W)

// code stored in the sketch: IRcomms.ino
//The IR communication components.
//
// Hacked together by Andrew Shirley

// Code which was either 'copypasta'ed or used as inspiration at some point:
//
// http://www.arduino.cc/cgi-bin/yabb2/YaBB.pl?num=1240843250 Copyright (C) Timo Herva aka 'mettapera', 2009
// http://tthheessiiss.wordpress.com/2009/08/05/dirt-cheap-wireless/ 

//NB. as these are quite time intensive enabling this often breaks it :-(
//#define DEBUG_SEND 1
//#define DEBUG_RECV 1

// pin numbers (9 is used for a Carrier wave and so isn't available)
#define pin_infrared 8 // ir LED
#define pin_ir_feedback 13 // normal LED
#define pin_ir_reciever_port PINB  // These 2 equate to pin 12
#define pin_ir_reciever_bit 4      // "           "          "
#define pin_ir_reciever 12         // normal LED

// some timings
long headerDuration = 2400;
long intervalDuration = 600;
long oneDuration = 1200;
long zeroDuration = 600;

byte timingTolerance = 100;

////////////////////////
// IR Writing variables
unsigned long writeBuffer = 0;
byte writeBits = 0;
unsigned long writeUpTime = 0;
unsigned long writeDownTime = 0;
unsigned long writeLastChangeTime = 0;

////////////////////////
// IR reading variables
unsigned long readBuffer = 0;
byte bitsRead = 0;

byte oldPinValue = 0;

//the micros for the point at which the IR went high
unsigned long readRiseTime = 0;

//the micros for the point at which the IR went low
unsigned long readFallTime = 0;

////////////////////////
// IR reading functions

//read the IR receiver and if applicable add to the readBuffer. This will return 1 if the transmission appears to be complete. Subsequent reads will return 0.
int signal_recieve() {
  byte pinValue = ! bitRead(pin_ir_reciever_port, pin_ir_reciever_bit);

  if (!oldPinValue && pinValue) {
    //IR rising edge
    readRiseTime = micros();
    oldPinValue = HIGH;
#ifdef DEBUG_RECV
    Serial.print("\\ @");
    Serial.println(readRiseTime);
#endif
    //there is always more to be read if the IR is high.
    return 0;
  }
  else if (oldPinValue && !pinValue) {
    //IR falling edge
    readFallTime = micros();
    unsigned long duration = readFallTime - readRiseTime;

    if (within_tolerance(duration, headerDuration, timingTolerance)) {
      //we are within tolerance of 2400 us - a restart
      readBuffer = 0;
      bitsRead = 0;
#ifdef DEBUG_RECV
      Serial.println("--");
#endif
    }
    else if (within_tolerance(duration, oneDuration, timingTolerance)) {
      //we are within tolerance of 1200 us - a one
      readBuffer = (readBuffer << 1) + 1;
      bitsRead++;
#ifdef DEBUG_RECV
      Serial.println("-1");
#endif
    }
    else if (within_tolerance(duration, zeroDuration, timingTolerance)) {
      //we are within tolerance of 600 us - a zero
      readBuffer = readBuffer << 1;
      bitsRead++;
#ifdef DEBUG_RECV
      Serial.println("-0");
#endif
    }
    else {
#ifdef DEBUG_RECV
      Serial.print("/ @");
      Serial.print(readFallTime);
      Serial.print("  ");
      Serial.println(duration);
#endif
    }

    oldPinValue = LOW;
    //wait to see if there is more to be read
    return 0;
  }
  else if (oldPinValue) {
    //IR continues to be high
    //there is always more to be read if the IR is high.
    return 0;
  }
  else /*if (!oldPinValue)*/ {
    //IR continues to be low
    //if we have been low for more than interval + tolerance (twice for extra leniency) we can assume the transmission has finished and try to read it.
    if (!readFallTime) {
      //we aren't waiting for an interval, all quiet on the IR front.
      return 0;
    }
    else if (micros() - readFallTime > intervalDuration + timingTolerance * 2) {
      readFallTime = 0; //cache this result
#ifdef DEBUG_RECV
      Serial.println("xx");
#endif
      return 1;
    }
    else {
      //still low, waiting for the interval
      return 0;
    }
  }
}

boolean within_tolerance(unsigned long value, unsigned long target, byte tolerance) {
  long remainder = value - target;
  return remainder < tolerance && remainder > -tolerance;
}

////////////////////////
// IR writing functions

void start_command(unsigned long command) {
  if (writeUpTime || writeDownTime) {
    //already writing - this is an error
    //Serial.println("tried to start a command when we are already sending");
    return;
  }

  command = reverse(command, 16);
  writeBuffer = addParityBit(command);
  writeBits = 17;

  //write header
  ir_up();
#ifdef DEBUG_SEND
  Serial.println("  \\");
#endif
  writeDownTime = headerDuration;
}

void signal_send() {
  unsigned long elapsed = micros() - writeLastChangeTime;
  
  if (writeDownTime && writeDownTime <= elapsed) {
#ifdef DEBUG_SEND
    Serial.print("  /");
    Serial.print(elapsed);
    Serial.print(" - ");
    Serial.println(writeDownTime, DEC);
#endif
    ir_down();
    writeDownTime = 0;
    
    if (writeBits) {
      //not done yet
      writeUpTime = intervalDuration;
    }
  }
  else if (writeUpTime && writeUpTime <= elapsed) {
#ifdef DEBUG_SEND
    Serial.print("  \\");
    Serial.print(elapsed);
    Serial.print(" - ");
    Serial.println(writeUpTime, DEC);
#endif
    ir_up();
    writeUpTime = 0;
    
    if (writeBuffer & B1) {
      //write a one
      writeDownTime = oneDuration;
    }
    else {
      //write a zero
      writeDownTime = zeroDuration;
    }
    
    writeBuffer = writeBuffer >> 1;
    writeBits--;
  }
}

void ir_up() {
  digitalWrite(pin_infrared, HIGH);
  digitalWrite(pin_ir_feedback, HIGH);
  writeLastChangeTime = micros();
}

void ir_down() {
  digitalWrite(pin_infrared, LOW);
  digitalWrite(pin_ir_feedback, LOW);
  writeLastChangeTime = micros();
}

/*
 * Reverse the num least significant bits.
 */
unsigned long reverse(unsigned long in, int num) {
  unsigned long out = 0;
  for (int i = 0; i < num; i++) {
    out = out << 1;
    out = out | (in & 1); //take the lsb from in to out
    in = in >> 1;
  }
  
  return out;
}

unsigned long timeCache = 0;

void timeDebug() {
  if (timeCache == 0) {
    timeCache = micros();
  }
  else {
    Serial.println(micros() - timeCache);
    timeCache = 0;
  }
}

// code stored in the sketch: main.ino
//#define DEBUG_DECODE 1

void decode_signal() {
#ifdef DEBUG_DECODE
  Serial.print("==");
  Serial.println(readBuffer, BIN);
  Serial.println(readBuffer, HEX);
#endif
}

//setting things ready
void setup() {
  //set the pins
  pinMode(pin_infrared, OUTPUT);
  pinMode(9, OUTPUT);
  pinMode(pin_ir_feedback, OUTPUT);
  pinMode(pin_ir_reciever, INPUT);
  
  // see http://www.atmel.com/dyn/resources/prod_documents/doc8161.pdf for more details (page 136 onwards)
  //set the carrier wave frequency. This only sets up pin 9.
  TCCR1A = _BV(COM1A0); // | _BV(COM1B0); for another pin (10)
  TCCR1B = _BV(WGM12) | _BV(CS10);
  
  TIMSK1 = 0; //no interupts
  TIFR1 = _BV(OCF1A) | _BV(OCF1A); //clear Output Compare Match Flags (by setting them :-P )
  unsigned long desired_freq = 40000;
  OCR1A = 10000000/desired_freq - 1; // see page 126 of datasheet for this equation
  //OCR1B = 10000000/desired_freq - 1; for another pin (10)

  ir_down();

  //debug  
  Serial.begin(9600);
}


unsigned long time = micros();

void loop() {
  if (micros() > time + 1000000) {
    time = micros();
    mt_fireShot();
  }

  signal_send();
  if (signal_recieve()) {
    decode_signal();
    mt_parseIRMessage(readBuffer);
  }
}

// code stored in the sketch: miles_tag_defines.ino

#define SYSTEM_MESSAGE                      B000

#define SYSTEM_MESSAGE_MASK                 0x1f00 // i.e. 5 least significant bits of the most significant byte
#define SYSTEM_MESSAGE_SHIFT                8

#define SYSTEM_MESSAGE_ADD_HEALTH           B00001
#define SYSTEM_MESSAGE_ADD_ROUNDS           B00010
#define SYSTEM_MESSAGE_ADD_CLIPS            B00011
#define SYSTEM_MESSAGE_ADD_RPG_ROUNDS       B00100

#define SYSTEM_MESSAGE_GOD_GUN              B01001

#define SYSTEM_MESSAGE_SCORE_DATA_HEADER    B10000
#define SYSTEM_MESSAGE_SCORE_REQUEST        B10001

#define SYSTEM_MESSAGE_SET_TEAM_ID          B10110
#define SYSTEM_MESSAGE_SET_PLAYER_ID        B10111

#define GOD_GUN_KILL_PLAYER                 0x00
#define GOD_GUN_PAUSE_PLAYER                0x01

#define GOD_GUN_START_GAME                  0x03
#define GOD_GUN_RESPAWN_PLAYER              0x04
#define GOD_GUN_INIT_PLAYER                 0x05
#define GOD_GUN_FULL_AMMO                   0x06
#define GOD_GUN_END_PLAYER                  0x07

#define UNLIMITED_CLIPS                     255
#define UNLIMITED_AMMO                      255


#define MT1_TEAM_MASK                       0xe000 // i.e. 3 most significant bits
#define MT1_TEAM_OFFSET                     13 // i.e. 3 most significant bits
#define MT1_PLAYER_MASK                     0x1f00 // i.e. 5 least significant bits of the most significant byte
#define MT1_PLAYER_OFFSET                   8 // i.e. 5 least significant bits of the most significant byte

#define MT1_DAMAGE_RESURRECT_OPPONENT       -1

// code stored in the sketch: miles_tag_gun_logic.ino
//milestag protocol 1 documented at http://www.lasertagparts.com/mtformat.htm
//milestag protocol 2 documented at http://www.lasertagparts.com/mtformat-2.htm
// we currently only implement MT1 as MT2 seems incomplete.

void serialPrint(int size, const char * fmt, ...) {
  char* out = (char*) malloc(size);
  va_list ap;
  va_start(ap, fmt);
  
  vsnprintf(out, size, fmt, ap);
  Serial.println(out);
  free(out);
  
  va_end (ap);
}

void mt_parseIRMessage(unsigned long recvBuffer) {
    if (!isEvenParity(recvBuffer)) {
        serialPrint(14, "Shot(Corrupt)");
        return;
    }

    //trim the 17th bit (parity) off to make things neater
    recvBuffer = recvBuffer >> 1;

    byte recv_TeamID = (recvBuffer & MT1_TEAM_MASK) >> MT1_TEAM_OFFSET;
    byte DataByte2 = recvBuffer & 0xff;

    if (recv_TeamID == SYSTEM_MESSAGE) {
        byte recv_SystemMessage = (recvBuffer & SYSTEM_MESSAGE_MASK) >> SYSTEM_MESSAGE_SHIFT;
        
        switch (recv_SystemMessage) {
            case SYSTEM_MESSAGE_SET_TEAM_ID:
                serialPrint(19, "Shot(SetTeam(%u))", DataByte2);
                break;
            case SYSTEM_MESSAGE_SET_PLAYER_ID:
                serialPrint(21, "Shot(SetPlayer(%u))", DataByte2);
                break;
            case SYSTEM_MESSAGE_ADD_HEALTH:
                serialPrint(21, "Shot(AddHealth(%u))", DataByte2);
                break;
            case SYSTEM_MESSAGE_ADD_CLIPS:
            {
                serialPrint(20, "Shot(AddClips(%u))", DataByte2);
                break;
            }
            case SYSTEM_MESSAGE_GOD_GUN:
            {
                byte recv_GodGun = DataByte2;
                switch (recv_GodGun) {
                    case GOD_GUN_KILL_PLAYER:
                        serialPrint(15, "Shot(Killed())");
                        break;
                    case GOD_GUN_FULL_AMMO:
                        serialPrint(17, "Shot(FullAmmo())");
                        break;
                    case GOD_GUN_RESPAWN_PLAYER:
                        serialPrint(15, "Shot(ReSpawn())");
                        break;
                    case GOD_GUN_PAUSE_PLAYER:
                    case GOD_GUN_START_GAME:
                    case GOD_GUN_INIT_PLAYER:
                    case GOD_GUN_END_PLAYER:
                    default:
                        serialPrint(17, "Shot(UnknownGGM)");
                        break;
                }
                
                break;
            }
            case SYSTEM_MESSAGE_ADD_ROUNDS:
                serialPrint(21, "Shot(AddRounds(%u))", DataByte2);
                break;
            case SYSTEM_MESSAGE_ADD_RPG_ROUNDS:
            case SYSTEM_MESSAGE_SCORE_DATA_HEADER:
            case SYSTEM_MESSAGE_SCORE_REQUEST:
            default:
                serialPrint(28, "Shot(UnknownSM(%lu))", recvBuffer);
                break;
        }
    } else {
        byte recv_PlayerID = (recvBuffer & MT1_PLAYER_MASK) >> MT1_PLAYER_OFFSET;
        signed char damage;
        
        byte recv_PlayerWeaponHit = DataByte2;
        switch (recv_PlayerWeaponHit) {
            case 0:
            {
                damage = MT1_DAMAGE_RESURRECT_OPPONENT;
                break;
            }
            case 1 ... 100:
            {
                damage = recv_PlayerWeaponHit;
                break;
            }
            //No 'Base' Mode
            /*case 101 ... 200:
            {
                recv_PlayerWeaponHit -= 100;
                baseDamage = recv_PlayerWeaponHit;
            }
            case 255:
                baseDamage = MT1_DAMAGE_RESURRECT_ENEMY_BASE;
            */

            default:
                serialPrint(17, "Shot(UnknownDmg)");
                break;
        }
        
        serialPrint(23, "Shot(Hit(%u,%u,%u))", recv_PlayerID, recv_TeamID, damage/*, baseDamage*/);
    }
}


void mt_fireShot() {
//  unsigned long shot = (TeamID << MT1_TEAM_OFFSET) | (PlayerID << MT1_PLAYER_OFFSET) | GunDamage;
  unsigned long shot = (0x01l << MT1_TEAM_OFFSET) | (0x01l << MT1_PLAYER_OFFSET) | 0x03l;

  //serialPrint(20, "shot: %ul", shot);

  start_command(shot);
}

// code stored in the sketch: parity.ino

boolean isEvenParity(unsigned long buf) {
  boolean evenParityBit = false;
  for (int i = 0; i < sizeof(unsigned long) * 8; i++) {
    evenParityBit = evenParityBit ^ (buf & 1);
    buf = buf >> 1;
  }
  return !evenParityBit;
}

unsigned long addParityBit(unsigned long in) {
  if (!isEvenParity(in)) {
    return in | 0x00010000;
  }
  else {
    return in;
  }
}
